// Logisim project gps-evaluator.circ as structural Verilog: 5 circuits, main circuit main
module main (
  output [7:0] out_1,
  output [7:0] out_2,
  output [7:0] out_3,
  output [7:0] out_4,
  output [7:0] out_5,
  output [7:0] out_6,
  output [7:0] out_7,
  output [7:0] out_8,
  output [7:0] out_9
);

  wire AND_out, Clock_2_out, Clock_out, Counter_2_sync, counter_3_carry, Counter_sync, GPS_Clock_out,
       not_1_out, not_2_out, OR_2_out, OR_out, uart_1_complete;
  wire [7:0] _4x8_Bit_Register_2_out_3, _4x8_Bit_Register_2_out_4, _4x8_Bit_Register_2_out_5,
       _4x8_Bit_Register_2_out_6, _4x8_Bit_Register_out_3, _4x8_Bit_Register_out_4, _4x8_Bit_Register_out_5,
       _4x8_Bit_Register_out_6, Shift_Buffer_out;
  wire [31:0] Counter_2_counter, Counter_counter;

  Clock #(.highDuration(3), .lowDuration(3)) Clock_2 (.out(Clock_2_out));
  Clock Clock (.out(Clock_out));
  Clock #(.highDuration(16), .lowDuration(16)) GPS_Clock (.out(GPS_Clock_out));
  counter Counter (
    .Clock(Clock_2_out), .Reference_Clock(GPS_Clock_out), .Counter(Counter_counter), .Sync(Counter_sync));
  counter Counter_2 (
    .Clock(Clock_out), .Reference_Clock(GPS_Clock_out), .Counter(Counter_2_counter), .Sync(Counter_2_sync));
  Counter #(.width(3), .max('h7)) counter_3 (
    .carry(counter_3_carry), .clk(not_1_out), .clr(OR_out));  // open: load, D, count, Q
  not not_1 (not_1_out, uart_1_complete);
  not not_2 (not_2_out, counter_3_carry);
  _4x8_register _4x8_Bit_Register (
    .in_1(Counter_counter), .Sync(Counter_sync), .out_3(_4x8_Bit_Register_out_3),
    .out_4(_4x8_Bit_Register_out_4), .out_5(_4x8_Bit_Register_out_5), .out_6(_4x8_Bit_Register_out_6));
  _4x8_register _4x8_Bit_Register_2 (
    .in_1(Counter_2_counter), .Sync(Counter_2_sync), .out_3(_4x8_Bit_Register_2_out_3),
    .out_4(_4x8_Bit_Register_2_out_4), .out_5(_4x8_Bit_Register_2_out_5), .out_6(_4x8_Bit_Register_2_out_6));
  or OR (OR_out, Counter_2_sync, Counter_sync);
  and AND (AND_out, not_2_out, uart_1_complete);
  or OR_2 (OR_2_out, OR_out, AND_out);
  Shift_Register #(.width(8)) Shift_Buffer (
    .in({8{1'b0}}), .clk(OR_2_out), .out(Shift_Buffer_out), .load(OR_out), .d0(_4x8_Bit_Register_2_out_6),
    .q0(out_9), .d1(_4x8_Bit_Register_2_out_5), .q1(out_8), .d2(_4x8_Bit_Register_2_out_4), .q2(out_7),
    .d3(_4x8_Bit_Register_2_out_3), .q3(out_6), .d4(_4x8_Bit_Register_out_6), .q4(out_5),
    .d5(_4x8_Bit_Register_out_5), .q5(out_4), .d6(_4x8_Bit_Register_out_4), .q6(out_3),
    .d7(_4x8_Bit_Register_out_3), .q7(out_2));  // open: shift, clr
  uart uart_1 (.Data(Shift_Buffer_out), .Trigger(OR_2_out), .out_3(out_1), .Complete(uart_1_complete));

  // Notes on the sheet:
  //   Data
  //   Sync
  //   Debug-Register
  //   Trigger
  //   Data
  //   Completed
endmodule

// Edge
module edge_detector (
  input  Signal,
  input  Clock,
  output Rising,
  output Falling
);

  wire not_1_out, not_2_out, Shift_q0, Shift_q1;

  Shift_Register #(.length(2)) Shift (
    .in(Signal), .clk(Clock), .q0(Shift_q0), .q1(Shift_q1));  // open: shift, out, load, clr, d0, d1
  not not_1 (not_1_out, Shift_q1);
  not not_2 (not_2_out, Shift_q0);
  and AND (Rising, not_1_out, Shift_q0);
  and AND_2 (Falling, Shift_q1, not_2_out);

  // Notes on the sheet:
  //   Clock: pull=down
  //   Signal: pull=down
endmodule

module counter (
  input  Clock,
  input  Reference_Clock,
  output [31:0] Counter,
  output Sync
);

  wire AND_out, edge_detector_1_rising, T_FF_q;

  T_Flip_Flop T_FF (.clk(Reference_Clock), .T(1'b1), .Q(T_FF_q));  // open: Qn, preset, reset, en
  and AND (AND_out, Clock, T_FF_q);
  edge_detector edge_detector_1 (.Signal(T_FF_q), .Clock(Clock), .Rising(edge_detector_1_rising), .Falling(Sync));
  Counter #(.width(32), .max('hffffffff)) u_Counter (
    .Q(Counter), .clk(AND_out), .clr(edge_detector_1_rising));  // open: load, D, count, carry

  // Notes on the sheet:
  //   Rising Edge
  //   Falling Edge
endmodule

module _4x8_register (
  input  [31:0] in_1,
  input  Sync,
  output [7:0] out_3,
  output [7:0] out_4,
  output [7:0] out_5,
  output [7:0] out_6
);

  wire [31:0] Register_q;

  BitSelector #(.width(32), .group(8)) bitselector_1 (.in(Register_q), .out(out_3), .sel(2'b11));
  BitSelector #(.width(32), .group(8)) bitselector_2 (.in(Register_q), .out(out_4), .sel(2'b10));
  BitSelector #(.width(32), .group(8)) bitselector_3 (.in(Register_q), .out(out_5), .sel(2'b01));
  Register #(.width(32)) Register (.D(in_1), .Q(Register_q), .clk(Sync));  // open: en, clr
  BitSelector #(.width(32), .group(8)) bitselector_4 (.in(Register_q), .out(out_6), .sel(2'b00));
endmodule

// UART
module uart (
  input  [7:0] Data,
  input  Trigger,
  output [7:0] out_3,
  output Complete
);

  wire clock_1_out;

  Clock clock_1 (.out(clock_1_out));
  edge_detector edge_detector_1 (.Signal(Trigger), .Clock(clock_1_out), .Falling(Complete));  // open: Rising
  Register register_1 (.D(Data), .Q(out_3), .clk(Complete));  // open: en, clr

  // Notes on the sheet:
  //   Complete: pull=down
  //   Trigger: pull=down
endmodule
